# Fritzing sketch 4-bit_ALU (saved by Fritzing 0.9.3b)
breadboards: 3

parts:
  U1 = 7427 3 x 3 Input NOR Gate [part_number=7427 package="DIP (Dual Inline) [THT]"]
  U2 = 7474 Dual Positive Edge Triggered D Flip Flop [part_number=7474 package="DIP (Dual Inline) [THT]"]
  U3 = 74161 4 Bit Synchronous Up Down Counter [part_number=74161 package="DIP16 [THT]"]

nets:
  GND: U1.GND, U2.GND, U3.GND
  VDD: U1.VDD, U2.VDD, U3.VCC

notes:
  Compute Unit:
  x1 4:1 MUX
  x3 2 Input XOR
  x4 2 Input NAND
  ----------------------
  Extra:
  x1 4:1 MUX
  x1 2 Input XOR
  *** 3 Chips ***
  Routing Unit:
  x2 4:1 MUX
  ----------------------
  Extra:
  *** 1 Chip ***
  Register Unit:
  x2 Shift Registers
  x4 2 Input NAND
  x2 2 Input XOR
  --------------------------
  Extra:
  *** 4 Chips ***
  Control Unit:
  x1 Counter
  x3 Triple Input NOR
  --------------------------
  Extra:
  *** 2 Chips ***

custom parts:
  7427 3 x 3 Input NOR Gate: 7427 3 x 2 Input NOR Gate
